# Fritzing sketch diagram (saved by Fritzing 0.9.4)
breadboards: 1

parts:
  MCU1 = Raspberry Pi Zero
  RHT1 = Humidity and Temperature Sensor RHT03
  RHT2 = Humidity and Temperature Sensor RHT03
  C1 = Ceramic Capacitor [capacitance=100nF package="100 mil [THT, multilayer]"]
  LED1 = LED - 5mm [color="Blue (430nm)" package="5 mm [THT]"]
  LED2 = LED - 5mm [color="Yellow (585nm)" package="5 mm [THT]"]
  Part1 = BME280 Breakout

nets:
  N1: MCU1.pin_1, MCU1.pin_17, C1.1, Part1.3.3V
  N2: MCU1.pin_3, Part1.SDI/SDA
  N3: MCU1.pin_5, Part1.SCK/SCL
  N4: MCU1.pin_6, MCU1.pin_9, MCU1.pin_14, MCU1.pin_34, RHT1.GND_2, C1.0, LED1.cathode, Part1.GND
  N5: MCU1.pin_11, RHT1.Data-signal
  N6: MCU1.pin_13, RHT1.Vcc
  N7: MCU1.pin_15, LED1.anode
  N8: MCU1.pin_29, RHT2.Data-signal
  N9: MCU1.pin_31, RHT2.Vcc
  N10: MCU1.pin_33, LED2.anode

notes:
  Actually BME280 (Pimoroni)
